// Logisim project pc.circ as structural Verilog: 7 circuits, main circuit main
module main (
);

  wire ALUO, and_1_out, AO, BO, Carry, CLK, CO, DO, JC, JMP, MO, or_1_out, RO, SA, SB, SC, SD,
       sevensegmentdriver_1_a, sevensegmentdriver_1_b, sevensegmentdriver_1_c, sevensegmentdriver_1_d,
       sevensegmentdriver_1_e, sevensegmentdriver_1_f, sevensegmentdriver_1_g, sevensegmentdriver_2_a,
       sevensegmentdriver_2_b, sevensegmentdriver_2_c, sevensegmentdriver_2_d, sevensegmentdriver_2_e,
       sevensegmentdriver_2_f, sevensegmentdriver_2_g, sevensegmentdriver_3_a, sevensegmentdriver_3_b,
       sevensegmentdriver_3_c, sevensegmentdriver_3_d, sevensegmentdriver_3_e, sevensegmentdriver_3_f,
       sevensegmentdriver_3_g, SM, SO, SRAL, SRAU, SROMAL, SROMAU;
  wire [3:0] doubledabble_1_hundreds, doubledabble_1_ones, doubledabble_1_tens;
  wire [7:0] ARegister_q, BRegister_q, CRegister_q, decodr_1_data, DRegister_q, eightbitadder_1_sum,
       OutputRegister, pull_resistor_8_node, ram_1_dout, RAMAddresRegisterLower_q, RAMAddresRegisterUpper_q;
  wire [11:0] countr_1_q;
  wire [15:0] rom_1_data, ROMAddress;
  wire [15:2] decodr_1_sflags;
  wire [15:6] decodr_1_oflags;

  Clock clock_1 (.out(CLK));
  _7_Segment_Display u_7_segment_display_1 (
    .g(sevensegmentdriver_1_g), .f(sevensegmentdriver_1_f), .a(sevensegmentdriver_1_a),
    .b(sevensegmentdriver_1_b), .e(sevensegmentdriver_1_e), .d(sevensegmentdriver_1_d),
    .c(sevensegmentdriver_1_c));  // open: dp
  _7_Segment_Display u_7_segment_display_2 (
    .g(sevensegmentdriver_2_g), .f(sevensegmentdriver_2_f), .a(sevensegmentdriver_2_a),
    .b(sevensegmentdriver_2_b), .e(sevensegmentdriver_2_e), .d(sevensegmentdriver_2_d),
    .c(sevensegmentdriver_2_c));  // open: dp
  _7_Segment_Display u_7_segment_display_3 (
    .g(sevensegmentdriver_3_g), .f(sevensegmentdriver_3_f), .a(sevensegmentdriver_3_a),
    .b(sevensegmentdriver_3_b), .e(sevensegmentdriver_3_e), .d(sevensegmentdriver_3_d),
    .c(sevensegmentdriver_3_c));  // open: dp
  SevenSegmentDriver sevensegmentdriver_1 (
    .in_1(doubledabble_1_hundreds), .F(sevensegmentdriver_1_f), .G(sevensegmentdriver_1_g),
    .A(sevensegmentdriver_1_a), .B(sevensegmentdriver_1_b), .C(sevensegmentdriver_1_c),
    .D(sevensegmentdriver_1_d), .E(sevensegmentdriver_1_e));
  SevenSegmentDriver sevensegmentdriver_2 (
    .in_1(doubledabble_1_tens), .F(sevensegmentdriver_2_f), .G(sevensegmentdriver_2_g),
    .A(sevensegmentdriver_2_a), .B(sevensegmentdriver_2_b), .C(sevensegmentdriver_2_c),
    .D(sevensegmentdriver_2_d), .E(sevensegmentdriver_2_e));
  SevenSegmentDriver sevensegmentdriver_3 (
    .in_1(doubledabble_1_ones), .F(sevensegmentdriver_3_f), .G(sevensegmentdriver_3_g),
    .A(sevensegmentdriver_3_a), .B(sevensegmentdriver_3_b), .C(sevensegmentdriver_3_c),
    .D(sevensegmentdriver_3_d), .E(sevensegmentdriver_3_e));
  DoubleDabble doubledabble_1 (
    .in_1(OutputRegister), .Ones(doubledabble_1_ones), .Tens(doubledabble_1_tens),
    .Hundreds(doubledabble_1_hundreds));
  and and_1 (and_1_out, JC, Carry);
  or or_1 (or_1_out, JMP, and_1_out);
  countr countr_1 (.LOAD(or_1_out), .CLK(CLK), .P(ROMAddress[11:0]), .Q(countr_1_q));
  Pull_Resistor pull_resistor_1 (.node(pull_resistor_8_node[6]));
  Pull_Resistor pull_resistor_2 (.node(pull_resistor_8_node[5]));
  Pull_Resistor pull_resistor_3 (.node(pull_resistor_8_node[4]));
  Pull_Resistor pull_resistor_4 (.node(pull_resistor_8_node[3]));
  Pull_Resistor pull_resistor_5 (.node(pull_resistor_8_node[7]));
  Pull_Resistor pull_resistor_6 (.node(pull_resistor_8_node[2]));
  Pull_Resistor pull_resistor_7 (.node(pull_resistor_8_node[1]));
  Pull_Resistor pull_resistor_8 (.node(pull_resistor_8_node[0]));
  ROM #(.addrWidth(12), .dataWidth(16)) rom_1 (.addr(countr_1_q), .data(rom_1_data));
  assign pull_resistor_8_node = RO ? decodr_1_data : 8'bz;  // Controlled_Buffer controlled_buffer_1
  assign pull_resistor_8_node = AO ? ARegister_q : 8'bz;  // Controlled_Buffer controlled_buffer_2
  assign pull_resistor_8_node = BO ? BRegister_q : 8'bz;  // Controlled_Buffer controlled_buffer_3
  assign pull_resistor_8_node = ALUO ? eightbitadder_1_sum : 8'bz;  // Controlled_Buffer controlled_buffer_4
  assign pull_resistor_8_node = CO ? CRegister_q : 8'bz;  // Controlled_Buffer controlled_buffer_5
  assign pull_resistor_8_node = DO ? DRegister_q : 8'bz;  // Controlled_Buffer controlled_buffer_6
  assign pull_resistor_8_node = MO ? ram_1_dout : 8'bz;  // Controlled_Buffer controlled_buffer_7
  EightBitRegstr ARegister (.Data(pull_resistor_8_node), .CLK(CLK), .Store(SA), .Q(ARegister_q));
  EightBitRegstr BRegister (.Data(pull_resistor_8_node), .CLK(CLK), .Store(SB), .Q(BRegister_q));
  EightBitRegstr CRegister (.Data(pull_resistor_8_node), .CLK(CLK), .Store(SC), .Q(CRegister_q));
  EightBitRegstr DRegister (.Data(pull_resistor_8_node), .CLK(CLK), .Store(SD), .Q(DRegister_q));
  EightBitRegstr RAMAddresRegisterLower (
    .Data(pull_resistor_8_node), .CLK(CLK), .Store(SRAL), .Q(RAMAddresRegisterLower_q));
  EightBitRegstr RAMAddresRegisterUpper (
    .Data(pull_resistor_8_node), .CLK(CLK), .Store(SRAU), .Q(RAMAddresRegisterUpper_q));
  EightBitRegstr ORegister (.Data(pull_resistor_8_node), .CLK(CLK), .Store(SO), .Q(OutputRegister));
  EightBitRegstr ROMAddressUpper (.Data(pull_resistor_8_node), .CLK(CLK), .Store(SROMAU), .Q(ROMAddress[7:0]));
  EightBitRegstr ROMAddressLower (.Data(pull_resistor_8_node), .CLK(CLK), .Store(SROMAL), .Q(ROMAddress[15:8]));
  decodr decodr_1 (
    .in_1(rom_1_data),
    .SFlags({decodr_1_sflags[15:14], SROMAU, SROMAL, SO, JC, JMP, SM, SRAU, SRAL, SD, SC, decodr_1_sflags[3:2], SB, SA}),
    .OFlags({decodr_1_oflags[15:9], MO, decodr_1_oflags[7:6], DO, CO, ALUO, RO, BO, AO}), .Data(decodr_1_data));
  EightBitAdder eightbitadder_1 (.B(ARegister_q), .A(BRegister_q), .CIN(1'b0), .Co(Carry), .SUM(eightbitadder_1_sum));
  RAM #(.addrWidth(16), .enables("line")) ram_1 (
    .addr({RAMAddresRegisterLower_q, RAMAddresRegisterUpper_q}), .we(SM), .clk(CLK),
    .din(pull_resistor_8_node), .dout(ram_1_dout));

  // Notes on the sheet:
  //   contents of rom_1 (hex, n*v repeats v):
  //   b0 102 10 d2 af b0 3 2d2 9f
endmodule

module countr (
  input  LOAD,
  input  CLK,
  input  [11:0] P,
  output [11:0] Q
);

  wire CARRY1, CARRY2, n74161_1_pin1, n74161_1_pin7, n74161_1_pin10, n74161_2_pin1, n74161_2_pin10,
       n74161_3_pin1, n74161_3_pin7, n74161_3_pin10, SPE;

  not not_1 (SPE, LOAD);
  _74161 u_74161_1 (
    .pin1(n74161_1_pin1), .pin2(CLK), .pin3(P[0]), .pin4(P[1]), .pin5(P[2]), .pin6(P[3]),
    .pin7(n74161_1_pin7), .pin15(CARRY1), .pin14(Q[0]), .pin13(Q[1]), .pin12(Q[2]), .pin11(Q[3]),
    .pin10(n74161_1_pin10), .pin9(SPE));
  _74161 u_74161_2 (
    .pin1(n74161_2_pin1), .pin2(CLK), .pin3(P[4]), .pin4(P[5]), .pin5(P[6]), .pin6(P[7]), .pin7(CARRY1),
    .pin15(CARRY2), .pin14(Q[4]), .pin13(Q[5]), .pin12(Q[6]), .pin11(Q[7]), .pin10(n74161_2_pin10), .pin9(SPE));
  _74161 u_74161_3 (
    .pin1(n74161_3_pin1), .pin2(CLK), .pin3(P[8]), .pin4(P[9]), .pin5(P[10]), .pin6(P[11]),
    .pin7(n74161_3_pin7), .pin14(Q[8]), .pin13(Q[9]), .pin12(Q[10]), .pin11(Q[11]), .pin10(n74161_3_pin10),
    .pin9(SPE));  // open: pin15
  and and_1 (n74161_3_pin7, CARRY1, CARRY2);
  // also tied to VCC on the sheet: {n74161_1_pin1, n74161_1_pin10, n74161_1_pin7, n74161_2_pin1, n74161_2_pin10, n74161_3_pin1, n74161_3_pin10}

  // Notes on the sheet:
  //   LOAD: pull=up
  //   CLK: pull=up
endmodule

module SevenSegmentDriver (
  input  [3:0] in_1,
  output F,
  output G,
  output A,
  output B,
  output C,
  output D,
  output E
);

  wire n7447_1_pin9, n7447_1_pin10, n7447_1_pin11, n7447_1_pin12, n7447_1_pin13, n7447_1_pin14, n7447_1_pin15;

  not not_1 (F, n7447_1_pin15);
  _7447 u_7447_1 (
    .pin1(in_1[1]), .pin2(in_1[2]), .pin6(in_1[3]), .pin7(in_1[0]), .pin15(n7447_1_pin15),
    .pin14(n7447_1_pin14), .pin13(n7447_1_pin13), .pin12(n7447_1_pin12), .pin11(n7447_1_pin11),
    .pin10(n7447_1_pin10), .pin9(n7447_1_pin9));  // open: pin3, pin4, pin5
  not not_2 (G, n7447_1_pin14);
  not not_3 (A, n7447_1_pin13);
  not not_4 (B, n7447_1_pin12);
  not not_5 (C, n7447_1_pin11);
  not not_6 (D, n7447_1_pin10);
  not not_7 (E, n7447_1_pin9);
endmodule

module DoubleDabble (
  input  [7:0] in_1,
  output [3:0] Ones,
  output [3:0] Tens,
  output [3:0] Hundreds
);

  wire sevensegmentdriver_1_a, sevensegmentdriver_1_b, sevensegmentdriver_1_c, sevensegmentdriver_1_d,
       sevensegmentdriver_1_e, sevensegmentdriver_1_f, sevensegmentdriver_1_g, sevensegmentdriver_2_a,
       sevensegmentdriver_2_b, sevensegmentdriver_2_c, sevensegmentdriver_2_d, sevensegmentdriver_2_e,
       sevensegmentdriver_2_f, sevensegmentdriver_2_g, sevensegmentdriver_3_a, sevensegmentdriver_3_b,
       sevensegmentdriver_3_c, sevensegmentdriver_3_d, sevensegmentdriver_3_e, sevensegmentdriver_3_f,
       sevensegmentdriver_3_g;
  wire [7:4] rom_2_data;

  ROM #(.addrWidth(13)) rom_1 (.addr({{5{1'b0}}, in_1}), .data({Tens, Ones}));
  ROM #(.addrWidth(13), .misaligned("true")) rom_2 (.addr({{5{1'b0}}, in_1}), .data({rom_2_data, Hundreds}));
  _7_Segment_Display u_7_segment_display_1 (
    .g(sevensegmentdriver_1_g), .f(sevensegmentdriver_1_f), .a(sevensegmentdriver_1_a),
    .b(sevensegmentdriver_1_b), .e(sevensegmentdriver_1_e), .d(sevensegmentdriver_1_d),
    .c(sevensegmentdriver_1_c));  // open: dp
  _7_Segment_Display u_7_segment_display_2 (
    .g(sevensegmentdriver_2_g), .f(sevensegmentdriver_2_f), .a(sevensegmentdriver_2_a),
    .b(sevensegmentdriver_2_b), .e(sevensegmentdriver_2_e), .d(sevensegmentdriver_2_d),
    .c(sevensegmentdriver_2_c));  // open: dp
  SevenSegmentDriver sevensegmentdriver_1 (
    .in_1(Hundreds), .F(sevensegmentdriver_1_f), .G(sevensegmentdriver_1_g), .A(sevensegmentdriver_1_a),
    .B(sevensegmentdriver_1_b), .C(sevensegmentdriver_1_c), .D(sevensegmentdriver_1_d),
    .E(sevensegmentdriver_1_e));
  _7_Segment_Display u_7_segment_display_3 (
    .g(sevensegmentdriver_3_g), .f(sevensegmentdriver_3_f), .a(sevensegmentdriver_3_a),
    .b(sevensegmentdriver_3_b), .e(sevensegmentdriver_3_e), .d(sevensegmentdriver_3_d),
    .c(sevensegmentdriver_3_c));  // open: dp
  SevenSegmentDriver sevensegmentdriver_2 (
    .in_1(Tens), .F(sevensegmentdriver_2_f), .G(sevensegmentdriver_2_g), .A(sevensegmentdriver_2_a),
    .B(sevensegmentdriver_2_b), .C(sevensegmentdriver_2_c), .D(sevensegmentdriver_2_d),
    .E(sevensegmentdriver_2_e));
  SevenSegmentDriver sevensegmentdriver_3 (
    .in_1(Ones), .F(sevensegmentdriver_3_f), .G(sevensegmentdriver_3_g), .A(sevensegmentdriver_3_a),
    .B(sevensegmentdriver_3_b), .C(sevensegmentdriver_3_c), .D(sevensegmentdriver_3_d),
    .E(sevensegmentdriver_3_e));

  // Notes on the sheet:
  //   in_1: pull=down
  //   Ones: pull=down
  //   Tens: pull=down
  //   Hundreds: pull=down
  //   contents of rom_1 (hex, n*v repeats v):
  //   0 1 2 3 4 5 6 7 8 9 10 11 12 13 14 15 16 17 18 19 20 21 22 23 24 25 26 27 28 29 30 31 32 33 34 35 36
  //   37 38 39 40 41 42 43 44 45 46 47 48 49 50 51 52 53 54 55 56 57 58 59 60 61 62 63 64 65 66 67 68 69
  //   70 71 72 73 74 75 76 77 78 79 80 81 82 83 84 85 86 87 88 89 90 91 92 93 94 95 96 97 98 99 0 1 2 3 4
  //   5 6 7 8 9 10 11 12 13 14 15 16 17 18 19 20 21 22 23 24 25 26 27 28 29 30 31 32 33 34 35 36 37 38 39
  //   40 41 42 43 44 45 46 47 48 49 50 51 52 53 54 55 56 57 58 59 60 61 62 63 64 65 66 67 68 69 70 71 72
  //   73 74 75 76 77 78 79 80 81 82 83 84 85 86 87 88 89 90 91 92 93 94 95 96 97 98 99 0 1 2 3 4 5 6 7 8 9
  //   10 11 12 13 14 15 16 17 18 19 20 21 22 23 24 25 26 27 28 29 30 31 32 33 34 35 36 37 38 39 40 41 42
  //   43 44 45 46 47 48 49 50 51 52 53 54 55
  //   contents of rom_2 (hex, n*v repeats v):
  //   100*0 100*1 56*2
endmodule

module EightBitRegstr (
  input  [7:0] Data,
  input  CLK,
  input  Store,
  output [7:0] Q
);

  wire controlled_buffer_1_out, controlled_buffer_2_out, controlled_buffer_3_out, controlled_buffer_4_out,
       controlled_buffer_5_out, controlled_buffer_6_out, controlled_buffer_7_out, controlled_buffer_8_out,
       d_ff_1_qn, d_ff_2_qn, d_ff_3_qn, d_ff_4_qn, d_ff_5_qn, d_ff_6_qn, d_ff_7_qn, d_ff_8_qn, not_2_out,
       not_3_out, not_4_out, not_5_out, not_6_out, not_7_out, not_8_out, not_9_out, Store_t;

  not not_1 (Store_t, Store);
  assign controlled_buffer_1_out = not_2_out ? Data[7] : 1'bz;  // Controlled_Buffer controlled_buffer_1
  not not_2 (not_2_out, Store_t);
  assign controlled_buffer_1_out = Store_t ? ~d_ff_1_qn : 1'bz;  // Controlled_Inverter controlled_inverter_1
  D_Flip_Flop d_ff_1 (.clk(CLK), .D(controlled_buffer_1_out), .Q(Q[7]), .Qn(d_ff_1_qn));  // open: preset, reset
  assign controlled_buffer_2_out = not_3_out ? Data[6] : 1'bz;  // Controlled_Buffer controlled_buffer_2
  not not_3 (not_3_out, Store_t);
  assign controlled_buffer_2_out = Store_t ? ~d_ff_2_qn : 1'bz;  // Controlled_Inverter controlled_inverter_2
  D_Flip_Flop d_ff_2 (.clk(CLK), .D(controlled_buffer_2_out), .Q(Q[6]), .Qn(d_ff_2_qn));  // open: preset, reset
  assign controlled_buffer_3_out = not_4_out ? Data[5] : 1'bz;  // Controlled_Buffer controlled_buffer_3
  not not_4 (not_4_out, Store_t);
  assign controlled_buffer_3_out = Store_t ? ~d_ff_3_qn : 1'bz;  // Controlled_Inverter controlled_inverter_3
  D_Flip_Flop d_ff_3 (.clk(CLK), .D(controlled_buffer_3_out), .Q(Q[5]), .Qn(d_ff_3_qn));  // open: preset, reset
  assign controlled_buffer_4_out = not_5_out ? Data[4] : 1'bz;  // Controlled_Buffer controlled_buffer_4
  not not_5 (not_5_out, Store_t);
  assign controlled_buffer_4_out = Store_t ? ~d_ff_4_qn : 1'bz;  // Controlled_Inverter controlled_inverter_4
  D_Flip_Flop d_ff_4 (.clk(CLK), .D(controlled_buffer_4_out), .Q(Q[4]), .Qn(d_ff_4_qn));  // open: preset, reset
  assign controlled_buffer_5_out = not_6_out ? Data[3] : 1'bz;  // Controlled_Buffer controlled_buffer_5
  not not_6 (not_6_out, Store_t);
  assign controlled_buffer_5_out = Store_t ? ~d_ff_5_qn : 1'bz;  // Controlled_Inverter controlled_inverter_5
  D_Flip_Flop d_ff_5 (.clk(CLK), .D(controlled_buffer_5_out), .Q(Q[3]), .Qn(d_ff_5_qn));  // open: preset, reset
  assign controlled_buffer_6_out = not_7_out ? Data[2] : 1'bz;  // Controlled_Buffer controlled_buffer_6
  not not_7 (not_7_out, Store_t);
  assign controlled_buffer_6_out = Store_t ? ~d_ff_6_qn : 1'bz;  // Controlled_Inverter controlled_inverter_6
  D_Flip_Flop d_ff_6 (.clk(CLK), .D(controlled_buffer_6_out), .Q(Q[2]), .Qn(d_ff_6_qn));  // open: preset, reset
  assign controlled_buffer_7_out = not_8_out ? Data[1] : 1'bz;  // Controlled_Buffer controlled_buffer_7
  not not_8 (not_8_out, Store_t);
  assign controlled_buffer_7_out = Store_t ? ~d_ff_7_qn : 1'bz;  // Controlled_Inverter controlled_inverter_7
  D_Flip_Flop d_ff_7 (.clk(CLK), .D(controlled_buffer_7_out), .Q(Q[1]), .Qn(d_ff_7_qn));  // open: preset, reset
  assign controlled_buffer_8_out = not_9_out ? Data[0] : 1'bz;  // Controlled_Buffer controlled_buffer_8
  not not_9 (not_9_out, Store_t);
  assign controlled_buffer_8_out = Store_t ? ~d_ff_8_qn : 1'bz;  // Controlled_Inverter controlled_inverter_8
  D_Flip_Flop d_ff_8 (.clk(CLK), .D(controlled_buffer_8_out), .Q(Q[0]), .Qn(d_ff_8_qn));  // open: preset, reset
endmodule

module EightBitAdder (
  input  [7:0] B,
  input  [7:0] A,
  input  CIN,
  output Co,
  output [7:0] SUM
);

  wire n74283_1_pin9;

  _74283 u_74283_1 (
    .pin1(SUM[1]), .pin2(B[1]), .pin3(A[1]), .pin4(SUM[0]), .pin5(A[0]), .pin6(B[0]), .pin7(CIN),
    .pin15(B[2]), .pin14(A[2]), .pin13(SUM[2]), .pin12(A[3]), .pin11(B[3]), .pin10(SUM[3]),
    .pin9(n74283_1_pin9));
  _74283 u_74283_2 (
    .pin1(SUM[5]), .pin2(B[5]), .pin3(A[5]), .pin4(SUM[4]), .pin5(A[4]), .pin6(B[4]), .pin7(n74283_1_pin9),
    .pin15(B[6]), .pin14(A[6]), .pin13(SUM[6]), .pin12(A[7]), .pin11(B[7]), .pin10(SUM[7]), .pin9(Co));

  // Other names for the same wires on the sheet: B_1[3:0] = A[7:4]; B_2[3:0] = B[7:4]
endmodule

module decodr (
  input  [15:0] in_1,
  output [15:0] SFlags,
  output [15:0] OFlags,
  output [7:0] Data
);

  wire n74138_1_pin4, n74138_1_pin6, n74138_1_pin7, n74138_1_pin9, n74138_1_pin10, n74138_1_pin11,
       n74138_1_pin12, n74138_1_pin13, n74138_1_pin14, n74138_1_pin15, n74138_2_pin4, n74138_2_pin6,
       n74138_2_pin7, n74138_2_pin9, n74138_2_pin10, n74138_2_pin11, n74138_2_pin12, n74138_2_pin13,
       n74138_2_pin14, n74138_2_pin15, n74138_3_pin7, n74138_3_pin9, n74138_3_pin10, n74138_3_pin11,
       n74138_3_pin12, n74138_3_pin13, n74138_3_pin14, n74138_3_pin15, n74138_4_pin7, n74138_4_pin9,
       n74138_4_pin10, n74138_4_pin11, n74138_4_pin12, n74138_4_pin13, n74138_4_pin14, n74138_4_pin15,
       n74240_1_pin1, n74240_2_pin1;

  _74138 u_74138_1 (
    .pin1(in_1[4]), .pin2(in_1[5]), .pin3(in_1[6]), .pin4(n74138_1_pin4), .pin5(n74138_1_pin4),
    .pin6(n74138_1_pin6), .pin7(n74138_1_pin7), .pin15(n74138_1_pin15), .pin14(n74138_1_pin14),
    .pin13(n74138_1_pin13), .pin12(n74138_1_pin12), .pin11(n74138_1_pin11), .pin10(n74138_1_pin10),
    .pin9(n74138_1_pin9));
  _74138 u_74138_2 (
    .pin1(in_1[0]), .pin2(in_1[1]), .pin3(in_1[2]), .pin4(n74138_2_pin4), .pin5(n74138_2_pin4),
    .pin6(n74138_2_pin6), .pin7(n74138_2_pin7), .pin15(n74138_2_pin15), .pin14(n74138_2_pin14),
    .pin13(n74138_2_pin13), .pin12(n74138_2_pin12), .pin11(n74138_2_pin11), .pin10(n74138_2_pin10),
    .pin9(n74138_2_pin9));
  not not_1 (n74138_1_pin6, in_1[7]);
  not not_2 (n74138_2_pin6, in_1[3]);
  _74138 u_74138_3 (
    .pin1(in_1[4]), .pin2(in_1[5]), .pin3(in_1[6]), .pin4(n74138_1_pin4), .pin5(n74138_1_pin4),
    .pin6(in_1[7]), .pin7(n74138_3_pin7), .pin15(n74138_3_pin15), .pin14(n74138_3_pin14),
    .pin13(n74138_3_pin13), .pin12(n74138_3_pin12), .pin11(n74138_3_pin11), .pin10(n74138_3_pin10),
    .pin9(n74138_3_pin9));
  _74138 u_74138_4 (
    .pin1(in_1[0]), .pin2(in_1[1]), .pin3(in_1[2]), .pin4(n74138_2_pin4), .pin5(n74138_2_pin4),
    .pin6(in_1[3]), .pin7(n74138_4_pin7), .pin15(n74138_4_pin15), .pin14(n74138_4_pin14),
    .pin13(n74138_4_pin13), .pin12(n74138_4_pin12), .pin11(n74138_4_pin11), .pin10(n74138_4_pin10),
    .pin9(n74138_4_pin9));
  _74240 u_74240_1 (
    .pin1(n74240_1_pin1), .pin2(n74138_1_pin15), .pin3(SFlags[6]), .pin4(n74138_1_pin14), .pin5(SFlags[5]),
    .pin6(n74138_1_pin13), .pin7(SFlags[4]), .pin8(n74138_1_pin7), .pin9(SFlags[3]), .pin19(n74240_1_pin1),
    .pin18(SFlags[0]), .pin17(n74138_1_pin9), .pin16(SFlags[1]), .pin15(n74138_1_pin10), .pin14(SFlags[2]),
    .pin13(n74138_1_pin11), .pin12(SFlags[7]), .pin11(n74138_1_pin12));
  _74240 u_74240_2 (
    .pin1(n74240_2_pin1), .pin2(n74138_2_pin15), .pin3(OFlags[6]), .pin4(n74138_2_pin14), .pin5(OFlags[5]),
    .pin6(n74138_2_pin13), .pin7(OFlags[4]), .pin8(n74138_2_pin7), .pin9(OFlags[3]), .pin19(n74240_2_pin1),
    .pin18(OFlags[0]), .pin17(n74138_2_pin9), .pin16(OFlags[1]), .pin15(n74138_2_pin10), .pin14(OFlags[2]),
    .pin13(n74138_2_pin11), .pin12(OFlags[7]), .pin11(n74138_2_pin12));
  _74240 u_74240_3 (
    .pin1(n74240_1_pin1), .pin2(n74138_3_pin7), .pin3(SFlags[14]), .pin4(n74138_3_pin15), .pin5(SFlags[13]),
    .pin6(n74138_3_pin14), .pin7(SFlags[12]), .pin8(n74138_3_pin13), .pin9(SFlags[11]),
    .pin19(n74240_1_pin1), .pin18(SFlags[15]), .pin17(n74138_3_pin9), .pin16(SFlags[8]),
    .pin15(n74138_3_pin10), .pin14(SFlags[9]), .pin13(n74138_3_pin11), .pin12(SFlags[10]),
    .pin11(n74138_3_pin12));
  _74240 u_74240_4 (
    .pin1(n74240_2_pin1), .pin2(n74138_4_pin7), .pin3(OFlags[14]), .pin4(n74138_4_pin15), .pin5(OFlags[13]),
    .pin6(n74138_4_pin14), .pin7(OFlags[12]), .pin8(n74138_4_pin13), .pin9(OFlags[11]),
    .pin19(n74240_2_pin1), .pin18(OFlags[15]), .pin17(n74138_4_pin9), .pin16(OFlags[8]),
    .pin15(n74138_4_pin10), .pin14(OFlags[9]), .pin13(n74138_4_pin11), .pin12(OFlags[10]),
    .pin11(n74138_4_pin12));

  assign Data = in_1[15:8];
  // also tied to GND on the sheet: {n74138_1_pin4, n74138_2_pin4, n74240_1_pin1, n74240_2_pin1}

  // Notes on the sheet:
  //   in_1: pull=down
endmodule
